// Logisim project ALU.circ as structural Verilog: 3 circuits, main circuit ALU
module ALU (
  input  [31:0] A,
  input  [31:0] B,
  input  [4:0] Shift,
  input  [3:0] Codop,
  input  CarryIn,
  output [31:0] S,
  output [3:0] Flags
);


  // Notes on the sheet:
  //   Note: for ROR, C = N
  //   premiere operande
  //   seconde operande
  //   nombre de decalage
  //   code operation ALU
  //   retenu entrente
  //   Note 2: assume that shift > 0 for LSL and LSR
  //   registre resultat
  //   registre drapeaux, ordre: NZCV
endmodule

module Addition32bits (
  input  [31:0] A,
  input  Cin,
  input  Cout,
  input  [31:0] B,
  output [31:0] S
);

  Adder #(.width(32)) adder_1 (.a(A), .b(B), .out(S), .cin(Cin), .cout(Cout));
endmodule

module Soustraction32bits (
  input  [31:0] A,
  input  Cin,
  input  Cout,
  input  [31:0] B,
  output [31:0] S
);

  Subtractor #(.width(32)) subtractor_1 (.a(A), .b(B), .out(S), .bin(Cin), .bout(Cout));
endmodule
