// Logisim project Ctl_Shift_Add_Sub_Mov.circ as structural Verilog: 2 circuits, main circuit Shift_Add_Sub_Mov
module Shift_Add_Sub_Mov (
  input  Enable,
  input  [15:0] Instruction,
  output [3:0] Flags_Update_Mask,
  output Carry,
  output Imm32_Enable,
  output [2:0] Rm,
  output [2:0] Rn,
  output [2:0] Rd,
  output [4:0] Imm5,
  output [31:0] Imm32,
  output [3:0] ALU_Opcode
);

  wire bit13, undriven;
  wire [31:0] bit_extender_1_out, bit_extender_2_out;

  // AND_Gate and_1 has open pins: in0=Enable, in1=undriven, out=open
  // AND_Gate and_2 is placed but not wired
  Bit_Extender #(.in_width(3), .out_width(32)) bit_extender_1 (.out(bit_extender_1_out));  // open: in
  Bit_Extender #(.out_width(32)) bit_extender_2 (.out(bit_extender_2_out));  // open: in
  Multiplexer #(.width(32)) multiplexer_1 (
    .in0(bit_extender_1_out), .in1(bit_extender_2_out), .out(Imm32), .sel(bit13));

  // Notes on the sheet:
  //   Pull output low on Enable = 0
  //   only ADD and SUB use Rm
  //   Enable carry for SUB since it is reversed in ALU
  //   ALU will use Imm32 instead of Rm
  //   Note: ALU uses Rn register for shifts. Use Rn instead of Rm for shifts (immediate) here too
  //   Note 2: MOV uses RSB ALU opcode with Imm8 reversed so that it is copied to output register
  //   Note 3: Imm32_Enable forces the use of the immediate for Rm register
endmodule

module Alu_Opcode (
  input  thirteen,
  input  twelve,
  input  eleven,
  input  ten,
  input  nine,
  output first,
  output second,
  output third,
  output forth
);

  wire and_1_out, and_2_out, and_3_out, and_4_out, and_5_out, and_6_out, and_7_out, and_8_out, and_9_out,
       and_10_out, and_11_out, not_1_out, not_2_out, not_3_out, not_4_out, not_5_out;

  not not_1 (not_1_out, thirteen);
  not not_2 (not_2_out, twelve);
  not not_3 (not_3_out, eleven);
  not not_4 (not_4_out, ten);
  not not_5 (not_5_out, nine);
  and and_1 (and_1_out, twelve, eleven, ten, nine);
  and and_2 (and_2_out, twelve, not_3_out);
  and and_3 (and_3_out, twelve, not_4_out);
  and and_4 (and_4_out, twelve, not_5_out);
  and and_5 (and_5_out, not_1_out, not_2_out);
  and and_6 (and_6_out, eleven, not_4_out, nine);
  and and_7 (and_7_out, eleven, ten, not_5_out);
  and and_8 (and_8_out, not_2_out, eleven);
  and and_9 (and_9_out, thirteen, not_3_out);
  and and_10 (and_10_out, not_1_out, not_2_out, eleven);
  and and_11 (and_11_out, not_1_out, eleven, not_5_out);
  or or_1 (first, thirteen, and_1_out);
  or or_2 (second, and_2_out, and_3_out, and_4_out);
  or or_3 (third, and_5_out, and_6_out, and_7_out, and_8_out);
  or or_4 (forth, and_9_out, and_10_out, and_11_out);
endmodule
